# Fritzing sketch Button and Encoder Connections Schematic (saved by Fritzing 0.9.4)
breadboards: 1

parts:
  Raspberry_Pi2 = Raspberry Pi B+
  Joint_A_Top = SWITCH-MOMENTARY-2 [package=tactile-switch-1101ne]
  Joint_A_Bottom = SWITCH-MOMENTARY-2 [package=tactile-switch-1101ne]
  Joint_B_Bottom = SWITCH-MOMENTARY-2 [package=tactile-switch-1101ne]
  Joint_B_Top = SWITCH-MOMENTARY-2 [package=tactile-switch-1101ne]
  Tilt_Encoder = AMT103
  Rotate_Encoder = AMT103
  Pan_Encoder = AMT103
  Emergency_Stop = SWITCH-MOMENTARY-2 [package=tactile-switch-1101ne]
  LED1 = LED - 5mm [color="Red (633nm)" package="5 mm [THT]"]  # not connected
  LED2 = LED - 5mm [color="Red (633nm)" package="5 mm [THT]"]  # not connected
  LED3 = LED - 5mm [color="Red (633nm)" package="5 mm [THT]"]  # not connected

nets:
  5V: Raspberry_Pi2.3v3, Tilt_Encoder.5V, Rotate_Encoder.5V, Pan_Encoder.5V
  N1: Raspberry_Pi2.GPIO17, Pan_Encoder.GND
  N2: Raspberry_Pi2.GPIO27, Pan_Encoder.X
  N3: Raspberry_Pi2.GPIO22, Pan_Encoder.A
  N4: Raspberry_Pi2.GPIO10, Rotate_Encoder.GND
  N5: Raspberry_Pi2.GPIO9, Rotate_Encoder.X
  N6: Raspberry_Pi2.GPIO11, Rotate_Encoder.A
  N7: Raspberry_Pi2.GPIO21, Tilt_Encoder.A
  N8: Raspberry_Pi2.GPIO20, Tilt_Encoder.X
  N9: Raspberry_Pi2.GPIO16, Tilt_Encoder.GND
  N10: Raspberry_Pi2.GPIO7, Joint_B_Bottom.1
  N11: Raspberry_Pi2.GPIO8, Joint_B_Top.1
  N12: Raspberry_Pi2.GPIO25, Emergency_Stop.1
  N13: Raspberry_Pi2.GPIO15, Joint_A_Bottom.1
  N14: Raspberry_Pi2.GPIO14, Joint_A_Top.1
  N15: Rotate_Encoder.B, Pan_Encoder.B
